# Fritzing sketch Untitled Sketch 2 (saved by Fritzing 1.0.1rc)
circuit board: 6.83919cm x 2.66949cm

parts:
  arduino_micro = Arduino Micro (Rev3)
  hc_06 = Bluetooth HC-05 Macho

nets:
  GND: arduino_micro.GND, hc_06.GND
  N1: arduino_micro.D10_PWM/A10, hc_06.TXD
  N2: arduino_micro.D11_PWM, hc_06.RXD
  3V3: arduino_micro.3V3, hc_06.VCC
