# Fritzing sketch carro (saved by Fritzing 0.9.3b)

parts:
  S1 = H-Bridge with L298N
  M1 = DC Motor
  Componente1 = Arduino Uno (Rev3)
  Componente2 = Bluetooth HC-05 Macho
  BAT1 = BC9VPC [package=bc9vpc]
  M2 = DC Motor

nets:
  N1: S1.12V, BAT1.V+
  GND: S1.GND, Componente1.GND, Componente2.GND, BAT1.V-
  N2: S1.IN1, Componente1.D2
  N3: S1.IN2, Componente1.D3_PWM
  N4: S1.IN3, Componente1.D4
  N5: S1.IN4, Componente1.D5_PWM
  N6: S1.OUT3-Motor2, M2.pin_2
  N7: S1.OUT4-Motor2, M2.pin_1
  N8: S1.OUT1-Motor1, M1.pin_1
  N9: S1.OUT2-Motor1, M1.pin_2
  N10: Componente1.D0/RX, Componente2.TXD
  N11: Componente1.D1/TX, Componente2.RXD
  5V: Componente1.5V, Componente2.VCC

custom parts:
  H-Bridge with L298N: h-bridge
