# Fritzing sketch Carro_arduino_version_PCB (saved by Fritzing 1.0.1rc)
circuit board: 3.59791cm x 5.57794cm

parts:
  Nano_v3 = Arduino Nano (Rev3.0)
  Hc_05 = Bluetooth HC-05 Macho
  L298N = PIC-ICSP [package=molex-1x6]
  servo = Dagu DGServo 9g header (male) [package=THT]
  Vin = Battery block 9V
  AMS = AMS11176 module
  LED1 = smd LED [color="Red (633nm)" package="1206 [SMD]"]

nets:
  GND: Nano_v3.GND, Hc_05.GND, L298N.PGM, servo.gnd, Vin.-, AMS.pin3, LED1.cathode
  N1: Nano_v3.D3, L298N.PGC
  N2: Nano_v3.D4, L298N.PGD
  N3: Nano_v3.D6, L298N.GND
  N4: Nano_v3.D7, L298N.VCC
  N5: Nano_v3.D10, servo.pulse
  N6: Nano_v3.D11/MOSI, Hc_05.RXD
  N7: Nano_v3.D12/MISO, Hc_05.TXD
  VIN: Nano_v3.VIN, servo.Vcc, AMS.pin2
  3V3: Nano_v3.3V3, Hc_05.VCC
  N8: Nano_v3.D13/SCK, LED1.anode
  N9: L298N.VPP, Vin.+, AMS.pin1

notes:
  v in1 in2  in3 in4 g
  - +
  s + -
  g o i
  v g
  smurillo29

custom parts:
  AMS11176 module: DC-DC step-down modules ( input DC 4.5～7V , output DC 3.3V ).
