# Fritzing sketch Carro_arduino_version_prototipo (saved by Fritzing 0.9.3b)
circuit board: 8.46667cm x 5.64444cm
perfboards: 1

parts:
  Componente1 = Arduino Nano (Rev3.0)
  S1 = H-Bridge with L298N
  R1 = Resistor [tolerance=±5% resistance=330 package="0805 [SMD]"]
  R2 = Resistor [tolerance=±5% resistance=330 package="0805 [SMD]"]
  R3 = Resistor [tolerance=±5% resistance=330 package="0805 [SMD]"]
  R4 = Resistor [tolerance=±5% resistance=330 package="0805 [SMD]"]
  LED4 = smd LED [color="Red (633nm)" package="0603 [SMD]"]
  LED5 = smd LED [color="Red (633nm)" package="0603 [SMD]"]
  LED6 = smd LED [color="Red (633nm)" package="0603 [SMD]"]
  R5 = Resistor [tolerance=±5% resistance=330 package="0805 [SMD]"]
  J1 = Piezo Speaker
  VCC1 = Battery block 9V
  M1 = DC Motor
  M2 = DC Motor
  Componente2 = Bluetooth HC-06
  LED3 = smd LED [color="Red (633nm)" package="0603 [SMD]"]

nets (from the breadboard view):
  GND: Componente1.GND, S1.GND, R1.Pin_1, R2.Pin_1, R3.Pin_1, R4.Pin_1, R5.Pin_1, VCC1.-, Componente2.GND
  N1: Componente1.D3, S1.IN4
  N2: Componente1.D4, S1.IN3
  N3: Componente1.D6, S1.IN2
  N4: Componente1.D7, S1.IN1
  N5: Componente1.D8, LED5.anode, LED6.anode
  N6: Componente1.D9, LED4.anode, LED3.anode
  N7: Componente1.D10, J1.pin2
  N8: Componente1.D11/MOSI, Componente2.RXD
  N9: Componente1.D12/MISO, Componente2.TXD
  VIN: Componente1.VIN, S1.12V, VCC1.+
  5V: Componente1.5V, Componente2.VCC
  N10: S1.OUT3-Motor2, M2.pin_2
  N11: S1.OUT4-Motor2, M2.pin_1
  N12: S1.OUT1-Motor1, M1.pin_1
  N13: S1.OUT2-Motor1, M1.pin_2
  N14: R1.Pin_0, LED5.cathode
  N15: R2.Pin_0, LED6.cathode
  N16: R3.Pin_0, LED4.cathode
  N17: R4.Pin_0, LED3.cathode
  N18: R5.Pin_0, J1.pin1

custom parts:
  H-Bridge with L298N: h-bridge
