# Fritzing sketch mbt (saved by Fritzing 0.9.3b)

parts:
  Componente1 = Bluetooth HC-06
  Componente2 = Arduino Uno (Rev3)

nets:
  N1: Componente1.RXD, Componente2.D1/TX
  N2: Componente1.TXD, Componente2.D0/RX
  GND: Componente1.GND, Componente2.GND
  VCC: Componente1.VCC, Componente2.5V
